# Fritzing sketch schema (saved by Fritzing 1.0.4)
breadboards: 1

parts:
  LED2 = LED - 3mm [color="Red (633nm)" current=0.030 package="3 mm [THT]"]
  LED3 = LED - 3mm [color="Red (633nm)" current=0.030 package="3 mm [THT]"]
  LED4 = LED - 3mm [color="Yellow (595nm)" current=0.030 package="3 mm [THT]"]
  R3 = Resistor [tolerance=±5% resistance=470 power=0.25 package=THT]
  R4 = Resistor [tolerance=±5% resistance=470 power=0.25 package=THT]
  BAT1 = LIPO-110mAh [package=lipo-110]
  ISP = Header 5x2 [package=avr_icsp]
  RE1 = KY-040 Rotary encoder [package="Breakout board"]
  Mod2 = 2S-BMS
  XTAL1 = CRYSTAL - kHz [frequency="32 kHz"]
  U1 = atmega328 [package=dip]
  Part1 = FTDI Basic Programmer
  U2 = MAX7219 [package=dil24]
  Disp1 = 20mm 8x8 dot matrix row cathode led display with narrow pcb pads
  R5 = Resistor [tolerance=±5% power=0.25W resistance=10k package=THT]
  R2 = Resistor [tolerance=±5% power=0.25 resistance=470 package=THT]
  R6 = Resistor [tolerance=±5% power=0.25W resistance=2.2k package=THT]
  R7 = Resistor [tolerance=±5% power=0.25W resistance=2.2k package=THT]
  R8 = Resistor [tolerance=±5% power=0.25W resistance=2.2k package=THT]
  C1 = Ceramic Capacitor [capacitance=68nF voltage=35V package="100 mil [THT, multilayer]"]
  C2 = Ceramic Capacitor [capacitance=68nF voltage=35V package="100 mil [THT, multilayer]"]
  C3 = Ceramic Capacitor [capacitance=68nF voltage=35V package="100 mil [THT, multilayer]"]
  R9 = Resistor [tolerance=±5% power=0.25 resistance=100 package=THT]
  Mod1 = Passive Buzzer

nets:
  N1: LED2.cathode, R2.Pin_1
  5V/VCC: LED2.anode, LED3.anode, LED4.anode, ISP.2, RE1.Vcc, Mod2.pin3#3, U1.VCC, U1.AVCC, U1.AREF, U2.VCC, R5.Pin_0
  N2: LED3.cathode, R3.Pin_1
  N3: LED4.cathode, R4.Pin_1
  N4: R3.Pin_0, U1.A1
  N5: R4.Pin_0, U1.A2
  N6: BAT1.+, Mod2.pin1
  N7: BAT1.-, Mod2.pin2
  MOSI: ISP.1, U1.D11_(PWM), U2.DIN
  GND: ISP.4, ISP.6, ISP.8, ISP.10, RE1.GND, Mod2.pin3#2, U1.GND, Part1.GND, U2.GND, U2.GND2, C1.1, C2.1, C3.1
  N8: ISP.5, U1.RESET
  SCK: ISP.7, U1.D13, U2.CLK
  MISO: ISP.9, U1.D12
  N9: RE1.SW, R6.Pin_0
  N10: RE1.DT, R7.Pin_0
  N11: RE1.CLK, R8.Pin_0
  N12: XTAL1.pin_0, U1.XLAT1
  N13: XTAL1.pin_1, U1.XLAT2
  N14: U1.D0_(RX), Part1.TXO
  N15: U1.D1_(TX), Part1.RXI
  N16: U1.D2, R8.Pin_1, C3.0
  N17: U1.D3_(PWM), R7.Pin_1, C2.0
  N18: U1.D4, R6.Pin_1, C1.0
  SS: U1.D8, U2.LOAD
  N19: U1.D9_(PWM), R9.Pin_1
  N20: U1.D10_(PWM), Mod1.-
  N21: U1.A0, R2.Pin_0
  N22: U2.DIG0, Disp1.pin_9
  N23: U2.DIG4, Disp1.pin_1
  N24: U2.DIG6, Disp1.pin_2
  N25: U2.DIG2, Disp1.pin_8
  N26: U2.DIG3, Disp1.pin_12
  N27: U2.DIG7, Disp1.pin_5
  N28: U2.DIG5, Disp1.pin_7
  N29: U2.DIG1, Disp1.pin_14
  N30: U2.SEGA, Disp1.pin_15
  N31: U2.SEGF, Disp1.pin_3
  N32: U2.SEGB, Disp1.pin_11
  N33: U2.SEGG, Disp1.pin_13
  N34: U2.ISET, R5.Pin_1
  N35: U2.SEGC, Disp1.pin_6
  N36: U2.SEGE, Disp1.pin_4
  N37: U2.SEGDP, Disp1.pin_16
  N38: U2.SEGD, Disp1.pin_10
  N39: R9.Pin_0, Mod1.S

notes:
  Test LEDs
  Programmer
  Audio out
  Rotary encoder
  BMS
  Debug UART
  LED matrix

custom parts:
  KY-040 Rotary encoder: KY-040 Rotary Encoder with switch on breakout borad from AZ Delivery
  2S-BMS: 2S-BMS LIPO battery charger / protection unit. Note pcb does not match the board as it will likely connect with wires, so pcb is 5 pads suitable for .1in header pins.
